// Logisim project rbuzby_hw9.circ as structural Verilog
module _4_1_decoder (
  input  S1,
  input  S0,
  output Out3,
  output Out2,
  output Out1,
  output Out0
);

  and and_1 (Out3, S0, S1);
  and and_2 (Out2, ~S0, S1);  // AND_Gate
  and and_3 (Out1, S0, ~S1);  // AND_Gate
  and and_4 (Out0, ~S0, ~S1);  // AND_Gate
endmodule

module palindrome (
  input  P4,
  input  P3,
  input  P2,
  input  P1,
  input  P0,
  output Out
);

  wire and_1_out, and_2_out, and_3_out, and_5_out, or_1_out, or_2_out;

  and and_1 (and_1_out, ~P4, ~P0);  // AND_Gate
  or or_1 (or_1_out, and_1_out, and_2_out);
  and and_2 (and_2_out, P4, P0);
  and and_3 (and_3_out, ~P3, ~P1);  // AND_Gate
  and and_4 (Out, or_1_out, or_2_out);
  and and_5 (and_5_out, P3, P1);
  or or_2 (or_2_out, and_3_out, and_5_out);
endmodule

module recognizer (
  input  In,
  output Out
);

  wire and_1_out, and_2_out, and_3_out, clear_out, clock_out, counter_1_q, d_ff_1_q, d_ff_2_q,
       demultiplexer_1_out0, demultiplexer_1_out1, not_1_out, shift_register_1_out, shift_register_2_out;

  and and_1 (and_1_out, d_ff_1_q, d_ff_2_q);
  Demultiplexer demultiplexer_1 (
    .out0(demultiplexer_1_out0), .out1(demultiplexer_1_out1), .in(In), .sel(counter_1_q));  // open: en
  Counter #(.width(1), .max('h1)) counter_1 (
    .D(clock_out), .Q(counter_1_q), .clk(clock_out), .clr(clear_out));  // open: load, count, carry
  Button clear (.out(clear_out));
  Button clock (.out(clock_out));
  D_Flip_Flop d_ff_1 (
    .clk(clock_out), .D(demultiplexer_1_out0), .Q(d_ff_1_q), .preset(and_3_out), .en(not_1_out),
    .reset(clear_out));  // open: Qn
  not not_1 (not_1_out, counter_1_q);
  and and_2 (and_2_out, ~d_ff_1_q, ~d_ff_2_q, shift_register_1_out);  // AND_Gate
  or or_1 (Out, and_1_out, and_2_out);
  D_Flip_Flop d_ff_2 (
    .clk(clock_out), .D(demultiplexer_1_out1), .Q(d_ff_2_q), .preset(and_3_out), .en(counter_1_q),
    .reset(clear_out));  // open: Qn
  and and_3 (and_3_out, Out, shift_register_2_out);
  Shift_Register #(.length(2)) shift_register_1 (
    .in(clock_out), .clk(clock_out), .out(shift_register_1_out), .clr(clear_out));  // open: shift, load, d0, q0, d1, q1
  Shift_Register #(.length(3)) shift_register_2 (
    .in(clock_out), .clk(clock_out), .out(shift_register_2_out), .clr(clear_out));  // open: shift, load, d0, q0, d1, q1, d2, q2
endmodule
